# Fritzing sketch start (saved by Fritzing 0.9.3b)

parts:
  R1 = Resistor [tolerance=±5% resistance=220 package=THT]
  S1 = Pushbutton [package="[THT]"]
  LED1 = LED - 5mm [color="Red (633nm)" package="5 mm [THT]"]
  S2 = SWITCH-MOMENTARY-2 [package=reed_switch_pth]
  VCC1 = Battery block 9V

nets:
  N1: R1.Pin_0, LED1.anode
  N2: R1.Pin_1, S1.Pin_3, S1.Pin_4, VCC1.+
  N3: LED1.cathode, S2.2
  N4: S2.1, VCC1.-
